// Logisim project cpu.circ as structural Verilog: 4 circuits, main circuit cpu
module cpu (
);

  wire clk, EQUAL_RESULT, half_mem, HALF_SELECT, isIMM, memload, memstore, registerfile_1_p16,
       registerfile_1_p17, regwrite_enable, RST;
  wire [1:0] PC_q, pcmux, regaddrmux, regdatamux;
  wire [3:0] aluop;
  wire [4:0] multiplexer_3_out, rs_addr, rt_addr;
  wire [5:0] funcode, opcode, PC_q_3;
  wire [15:0] \总周期数 , \无条件分支指令数 , \有条件分支成功跳转 , \有条件分支指令数 ;
  wire [15:6] imm16;
  wire [23:0] PC_q_2;
  wire [31:0] adder_1_out, adder_2_out, alu_out, bit_extender_1_out, bit_extender_2_out, bit_extender_3_out,
       mem_out, mips_ram_1_p7, multiplexer_1_out, multiplexer_2_out, multiplexer_4_out, registerfile_1_p13,
       registerfile_1_p14, SyscallOut;

  Button \u_总复位  (.out(RST));
  Hex_Digit_Display hex_digit_display_1 (.value(SyscallOut[27:24]));  // open: dp
  Hex_Digit_Display hex_digit_display_2 (.value(SyscallOut[31:28]));  // open: dp
  Hex_Digit_Display hex_digit_display_3 (.value(SyscallOut[23:20]));  // open: dp
  Hex_Digit_Display hex_digit_display_4 (.value(SyscallOut[19:16]));  // open: dp
  Adder #(.width(32)) adder_1 (.a(32'h4), .b({PC_q_3, PC_q_2, PC_q}), .out(adder_1_out));  // open: cin, cout
  Hex_Digit_Display hex_digit_display_5 (.value(SyscallOut[15:12]));  // open: dp
  Hex_Digit_Display hex_digit_display_6 (.value(SyscallOut[11:8]));  // open: dp
  Adder #(.width(32)) adder_2 (
    .a(adder_1_out), .b({{14{1'b0}}, imm16, funcode, 2'b00}), .out(adder_2_out));  // open: cin, cout
  Hex_Digit_Display hex_digit_display_7 (.value(SyscallOut[7:4]));  // open: dp
  Hex_Digit_Display hex_digit_display_8 (.value(SyscallOut[3:0]));  // open: dp
  Multiplexer #(.select(2), .width(32), .enable("false")) multiplexer_1 (
    .in0(adder_1_out), .in1(registerfile_1_p13), .in2(adder_2_out),
    .in3({{6{1'b0}}, rs_addr[2:0], rt_addr, imm16, funcode, 2'b00}), .out(multiplexer_1_out), .sel(pcmux));
  Register #(.width(32)) PC (.D(multiplexer_1_out), .Q({PC_q_3, PC_q_2, PC_q}), .clk(clk));  // open: en, clr
  // Probe on \总周期数 
  // Probe on \无条件分支指令数 
  // Probe on \有条件分支指令数 
  // Probe on \有条件分支成功跳转 
  ROM #(.addrWidth(24), .dataWidth(32)) rom_1 (
    .addr(PC_q_2), .data({opcode, rs_addr, rt_addr, imm16, funcode}));  // open: sel
  assign bit_extender_1_out = {{16{imm16[15]}}, {imm16, funcode}};  // Bit_Extender bit_extender_1
  Multiplexer #(.select(2), .width(32), .disabled(0), .enable("false")) multiplexer_2 (
    .in0(alu_out), .in1({PC_q_3, PC_q_2, PC_q}), .in2(mem_out), .out(multiplexer_2_out), .sel(regdatamux));  // open: in3
  Multiplexer #(.select(2), .width(5), .enable("false")) multiplexer_3 (
    .in0(imm16[15:11]), .in1(rt_addr), .in2({5{1'b1}}), .out(multiplexer_3_out), .sel(regaddrmux));  // open: in3
  Clock clock_1 (.out(clk));
  // RegisterFile registerfile_1: pin names not known; wires that end beside it: pcmux, isIMM, memstore, memload, half_mem, aluop, multiplexer_2_out, clk, regwrite_enable, multiplexer_3_out, rs_addr, rt_addr, registerfile_1_p13, registerfile_1_p14, registerfile_1_p14, registerfile_1_p16, registerfile_1_p17
  Multiplexer #(.width(32), .enable("false")) multiplexer_4 (
    .in0(registerfile_1_p14), .in1(bit_extender_1_out), .out(multiplexer_4_out), .sel(isIMM));
  ALU alu_1 (
    .AluOP(aluop), .X(registerfile_1_p13), .Equal(EQUAL_RESULT), .Result(alu_out),
    .Signed_Overflow(registerfile_1_p16), .Y(multiplexer_4_out), .UnSigned_Overflow(registerfile_1_p17),
    .shamt(imm16[10:6]));  // open: Result_2
  // MIPS_RAM mips_ram_1: pin names not known; wires that end beside it: alu_out[25:2], registerfile_1_p13, memstore, clk, memload, RST, mips_ram_1_p7, alu_out[1], HALF_SELECT
  assign bit_extender_2_out = {{16{1'b0}}, mips_ram_1_p7[15:0]};  // Bit_Extender bit_extender_2
  assign bit_extender_3_out = {{16{1'b0}}, mips_ram_1_p7[31:16]};  // Bit_Extender bit_extender_3
  Multiplexer #(.select(2), .width(32), .enable("false")) multiplexer_5 (
    .in0(mips_ram_1_p7), .in2(bit_extender_2_out), .in3(bit_extender_3_out), .out(mem_out),
    .sel({half_mem, HALF_SELECT}));  // open: in1

  // Other names for the same wires on the sheet: imm16[5:0] = funcode; shamt[4:0] = imm16[10:6];
  //   rd_addr[4:0] = imm16[15:11]; CMP_RESULT = alu_out[0]

  // Notes on the sheet:
  //   数码管输出应该用寄存器锁存，否则显示数据只能一闪而过
  //   可以通过项目增加Logisim库的方式将前几次实验完成的电路作为子电路引入到本电路中使用
  //   数码管输出
  //   总复位信号应将除ROM以外所有存储组件全部清零
endmodule

module controller (
  input  [5:0] opcode,
  input  [5:0] funcode
);

  wire comparator_1_eq;
  wire [3:0] aluop, fun2alu_1_out_2, op2alu_1_out_2;

  op2alu op2alu_1 (.funcode(opcode), .out_2(op2alu_1_out_2));
  Comparator #(.width(6), .mode("unsigned")) comparator_1 (
    .a(opcode), .b({6{1'b0}}), .eq(comparator_1_eq));  // open: gt, lt
  fun2alu fun2alu_1 (.funcode(funcode), .out_2(fun2alu_1_out_2));
  Multiplexer #(.width(4), .enable("false")) multiplexer_1 (
    .in0(op2alu_1_out_2), .in1(fun2alu_1_out_2), .out(aluop), .sel(comparator_1_eq));
endmodule

module op2alu (
  input  [5:0] funcode,
  output [3:0] out_2
);

  wire and_1_out, and_2_out, and_3_out, and_4_out, and_5_out, and_6_out, and_7_out, not_1_out, not_2_out,
       not_3_out, not_4_out, not_5_out, not_6_out, not_7_out, not_8_out, not_9_out, or_1_out, or_2_out;

  not not_1 (not_1_out, funcode[5]);
  or or_1 (or_1_out, not_1_out, funcode[2]);
  or or_2 (or_2_out, not_1_out, funcode[1]);
  not not_2 (not_2_out, funcode[0]);
  not not_3 (not_3_out, or_2_out);
  not not_4 (not_4_out, funcode[0]);
  not not_5 (not_5_out, or_1_out);
  not not_6 (not_6_out, funcode[0]);
  not not_7 (not_7_out, funcode[0]);
  not not_8 (not_8_out, or_1_out);
  not not_9 (not_9_out, funcode[0]);
  and and_1 (and_1_out, or_2_out, not_2_out);
  or or_3 (out_2[3], and_1_out, and_2_out);
  and and_2 (and_2_out, or_1_out, funcode[0]);
  and and_3 (and_3_out, not_3_out, not_4_out);
  or or_4 (out_2[2], and_3_out, and_4_out);
  and and_4 (and_4_out, not_5_out, funcode[0]);
  and and_5 (and_5_out, or_2_out, not_6_out);
  or or_5 (out_2[1], and_5_out, and_6_out, and_7_out);
  and and_6 (and_6_out, or_1_out, not_7_out);
  and and_7 (and_7_out, or_1_out, or_2_out);
  or or_6 (out_2[0], not_8_out, not_9_out, or_2_out);
endmodule

module fun2alu (
  input  [5:0] funcode,
  output [3:0] out_2
);

  wire and_1_out, and_2_out, and_3_out, and_4_out, and_5_out, and_6_out, and_7_out, and_8_out, and_9_out,
       and_10_out, and_11_out, not_1_out, not_2_out, not_3_out, not_4_out, not_5_out, not_6_out, not_7_out,
       not_8_out, not_9_out, not_10_out, not_11_out, not_12_out, not_13_out, not_14_out, not_15_out,
       not_16_out, not_17_out, or_1_out, or_2_out;

  not not_1 (not_1_out, funcode[5]);
  or or_1 (or_1_out, not_1_out, funcode[3]);
  or or_2 (or_2_out, not_1_out, funcode[2]);
  not not_2 (not_2_out, or_1_out);
  not not_3 (not_3_out, or_2_out);
  not not_4 (not_4_out, or_1_out);
  not not_5 (not_5_out, funcode[0]);
  not not_6 (not_6_out, or_2_out);
  not not_7 (not_7_out, or_1_out);
  not not_8 (not_8_out, funcode[0]);
  not not_9 (not_9_out, or_1_out);
  not not_10 (not_10_out, funcode[0]);
  not not_11 (not_11_out, or_1_out);
  not not_12 (not_12_out, funcode[1]);
  not not_13 (not_13_out, funcode[0]);
  not not_14 (not_14_out, or_2_out);
  not not_15 (not_15_out, funcode[1]);
  not not_16 (not_16_out, or_2_out);
  not not_17 (not_17_out, funcode[0]);
  and and_1 (and_1_out, not_2_out, or_2_out, funcode[0]);
  or or_3 (out_2[3], and_1_out, and_2_out);
  and and_2 (and_2_out, or_1_out, not_3_out);
  and and_3 (and_3_out, not_4_out, not_5_out);
  or or_4 (out_2[2], and_3_out, and_4_out);
  and and_4 (and_4_out, not_6_out, funcode[0]);
  and and_5 (and_5_out, not_7_out, funcode[1]);
  and and_6 (and_6_out, funcode[1], not_8_out);
  or or_5 (out_2[1], and_5_out, and_6_out, and_7_out);
  and and_7 (and_7_out, not_9_out, or_2_out, not_10_out);
  and and_8 (and_8_out, not_11_out, not_12_out, not_13_out);
  and and_9 (and_9_out, not_14_out, not_15_out);
  and and_10 (and_10_out, or_1_out, not_16_out, not_17_out);
  and and_11 (and_11_out, or_1_out, or_2_out, funcode[0]);
  or or_6 (out_2[0], and_8_out, and_9_out, and_10_out, and_11_out);
endmodule
