// Logisim project cpu_benchmark.circ as structural Verilog: 4 circuits, main circuit cpu
module cpu (
);

  wire clk, comparator_1_eq, controller_1_cond_jmp, controller_1_succ_cond_jmp, controller_1_uncond_jmp,
       d_ff_1_qn, display, EQUAL_RESULT, half_mem, halt, isIMM, memload, memstore, not_1_out,
       registerfile_1_p10, registerfile_1_p11, regwrite_enable, RST, syscall;
  wire [1:0] PC_q, pcmux, regaddrmux, regdatamux;
  wire [3:0] aluop;
  wire [4:0] multiplexer_3_out, multiplexer_4_out, multiplexer_5_out;
  wire [5:0] funcode, opcode, PC_q_3;
  wire [15:0] \总周期数 , \无条件分支指令数 , \有条件分支成功跳转 , \有条件分支指令数 ;
  wire [19:0] code20;
  wire [23:0] PC_q_2;
  wire [31:0] adder_1_out, adder_2_out, alu_out, bit_extender_1_out, bit_extender_2_out, bit_extender_3_out,
       bit_extender_4_out, mem_out, mips_ram_1_p7, multiplexer_1_out, multiplexer_2_out, multiplexer_6_out,
       registerfile_1_p7, registerfile_1_p8, SyscallOut;

  Button \u_总复位  (.out(RST));
  Hex_Digit_Display hex_digit_display_1 (.value(SyscallOut[31:28]));  // open: dp
  Hex_Digit_Display hex_digit_display_2 (.value(SyscallOut[27:24]));  // open: dp
  Hex_Digit_Display hex_digit_display_3 (.value(SyscallOut[23:20]));  // open: dp
  Hex_Digit_Display hex_digit_display_4 (.value(SyscallOut[19:16]));  // open: dp
  // Probe on aluop
  Adder #(.width(32)) adder_1 (.a(32'h4), .b({PC_q_3, PC_q_2, PC_q}), .out(adder_1_out));  // open: cin, cout
  Hex_Digit_Display hex_digit_display_5 (.value(SyscallOut[11:8]));  // open: dp
  Hex_Digit_Display hex_digit_display_6 (.value(SyscallOut[15:12]));  // open: dp
  // Probe on code20[4:0]
  // Probe on pcmux
  Adder #(.width(32)) adder_2 (.a(adder_1_out), .b(bit_extender_1_out), .out(adder_2_out));  // open: cin, cout
  Hex_Digit_Display hex_digit_display_7 (.value(SyscallOut[7:4]));  // open: dp
  Hex_Digit_Display hex_digit_display_8 (.value(SyscallOut[3:0]));  // open: dp
  // Probe on code20[14:10]
  not not_1 (not_1_out, halt);
  Multiplexer #(.select(2), .width(32), .enable("false")) multiplexer_1 (
    .in0(adder_1_out), .in1(registerfile_1_p7), .in2(adder_2_out),
    .in3({{6{1'b0}}, code20[17:0], funcode, 2'b00}), .out(multiplexer_1_out), .sel(pcmux));
  // Probe on code20[19:15]
  Register #(.width(32)) PC (.D(multiplexer_1_out), .en(not_1_out), .Q({PC_q_3, PC_q_2, PC_q}), .clk(clk), .clr(RST));
  assign bit_extender_1_out = {{14{code20[9]}}, {code20[9:0], funcode, 2'b00}};  // Bit_Extender bit_extender_1
  // Probe on \总周期数 
  // Probe on \无条件分支指令数 
  // Probe on \有条件分支指令数 
  // Probe on \有条件分支成功跳转 
  Clock clock_1 (.out(clk));
  ROM #(.addrWidth(24), .dataWidth(32)) rom_1 (.addr(PC_q_2), .data({opcode, code20, funcode}));  // open: sel
  controller controller_1 (
    .opcode(opcode), .funcode(funcode), .CMP_RESULT(alu_out[0]), .EQUAL_RESULT(EQUAL_RESULT),
    .regdatamux(regdatamux), .regaddrmux(regaddrmux), .regwrite_enable(regwrite_enable), .pcmux(pcmux),
    .isIMM(isIMM), .memstore(memstore), .memload(memload), .half_mem(half_mem), .alu_op(aluop),
    .syscall(syscall), .uncond_jmp(controller_1_uncond_jmp), .cond_jmp(controller_1_cond_jmp),
    .succ_cond_jmp(controller_1_succ_cond_jmp));
  // Probe on code20[4:0]
  assign bit_extender_2_out = {{16{code20[9]}}, {code20[9:0], funcode}};  // Bit_Extender bit_extender_2
  Counter #(.width(16), .max('hffff)) counter_1 (
    .count(controller_1_succ_cond_jmp), .Q(\有条件分支成功跳转 ), .clk(clk), .clr(RST));  // open: load, D, carry
  Counter #(.width(16), .max('hffff)) counter_2 (
    .count(controller_1_uncond_jmp), .Q(\无条件分支指令数 ), .clk(clk), .clr(RST));  // open: load, D, carry
  Multiplexer #(.select(2), .width(32), .disabled(0), .enable("false")) multiplexer_2 (
    .in0(alu_out), .in1(adder_1_out), .in2(mem_out), .out(multiplexer_2_out), .sel(regdatamux));  // open: in3
  Multiplexer #(.width(5), .enable("false")) multiplexer_3 (
    .in0(code20[19:15]), .in1(5'b00100), .out(multiplexer_3_out), .sel(syscall));
  Multiplexer #(.width(5), .enable("false")) multiplexer_4 (
    .in0(code20[14:10]), .in1(5'b00010), .out(multiplexer_4_out), .sel(syscall));
  Multiplexer #(.select(2), .width(5), .enable("false")) multiplexer_5 (
    .in0(code20[9:5]), .in1(code20[14:10]), .in2({5{1'b1}}), .out(multiplexer_5_out), .sel(regaddrmux));  // open: in3
  Counter #(.width(16), .max('hffff)) counter_3 (
    .count(controller_1_cond_jmp), .Q(\有条件分支指令数 ), .clk(clk), .clr(RST));  // open: load, D, carry
  // RegisterFile registerfile_1: pin names not known; wires that end beside it: multiplexer_2_out, clk, regwrite_enable, multiplexer_5_out, multiplexer_3_out, multiplexer_4_out, registerfile_1_p7, registerfile_1_p8, registerfile_1_p8, registerfile_1_p10, registerfile_1_p11
  // Probe on registerfile_1_p8
  Register #(.width(32)) register_1 (.D(registerfile_1_p7), .en(display), .Q(SyscallOut), .clk(clk), .clr(RST));
  Comparator #(.width(32), .mode("unsigned")) comparator_1 (
    .a(32'ha), .b(registerfile_1_p8), .eq(comparator_1_eq));  // open: gt, lt
  // Probe on registerfile_1_p7
  Multiplexer #(.width(32), .enable("false")) multiplexer_6 (
    .in0(registerfile_1_p8), .in1(bit_extender_2_out), .out(multiplexer_6_out), .sel(isIMM));
  // Probe on multiplexer_6_out
  Demultiplexer #(.disabled(0), .enable("false")) demultiplexer_1 (
    .out0(display), .out1(halt), .in(syscall), .sel(comparator_1_eq));
  ALU alu_1 (
    .AluOP(aluop), .X(registerfile_1_p7), .Equal(EQUAL_RESULT), .Result(alu_out),
    .Signed_Overflow(registerfile_1_p10), .Y(multiplexer_6_out), .UnSigned_Overflow(registerfile_1_p11),
    .shamt(code20[4:0]));  // open: Result_2
  // MIPS_RAM mips_ram_1: pin names not known; wires that end beside it: alu_out[25:2], registerfile_1_p8, memstore, clk, memload, RST, mips_ram_1_p7
  D_Flip_Flop d_ff_1 (.clk(clk), .D(halt), .Qn(d_ff_1_qn), .reset(RST));  // open: Q, preset, en
  // Probe on alu_out
  Counter #(.width(16), .max('hffff)) counter_4 (
    .count(d_ff_1_qn), .Q(\总周期数 ), .clk(clk), .clr(RST));  // open: load, D, carry
  assign bit_extender_3_out = {{16{mips_ram_1_p7[15]}}, mips_ram_1_p7[15:0]};  // Bit_Extender bit_extender_3
  assign bit_extender_4_out = {{16{mips_ram_1_p7[31]}}, mips_ram_1_p7[31:16]};  // Bit_Extender bit_extender_4
  Multiplexer #(.select(2), .width(32), .enable("false")) multiplexer_7 (
    .in0(mips_ram_1_p7), .in2(bit_extender_3_out), .in3(bit_extender_4_out), .out(mem_out),
    .sel({half_mem, alu_out[1]}));  // open: in1

  // Other names for the same wires on the sheet: imm16[15:0] = {code20[9:0], funcode}; shamt[4:0] = code20[4:0];
  //   rd_addr[4:0] = code20[9:5]; rt_addr[4:0] = code20[14:10]; rs_addr[4:0] = code20[19:15];
  //   HALF_SELECT = alu_out[1]; CMP_RESULT = alu_out[0]

  // Notes on the sheet:
  //   数码管输出应该用寄存器锁存，否则显示数据只能一闪而过
  //   可以通过项目增加Logisim库的方式将前几次实验完成的电路作为子电路引入到本电路中使用
  //   数码管输出
  //   总复位信号应将除ROM以外所有存储组件全部清零
  //   contents of rom_1 (hex, n*v repeats v):
  //   20110001 8000005 20110001 20120002 20130003 8000009 20110001 20120002 20130003 800000d 20110001
  //   20120002 20130003 8000011 20110001 20120002 20130003 c0000b8 20100001 20110001 118fc0 112020
  //   20020022 c 118882 12200001 8000015 112020 20020022 c 20110001 118880 112020 20020022 c 12200001
  //   800001f 20110001 118fc0 112020 20020022 c 1188c3 112020 20020022 c 118903 112020 20020022 c 118903
  //   112020 20020022 c 118903 112020 20020022 c 118903 112020 20020022 c 118903 112020 20020022 c 118903
  //   112020 20020022 c 118903 112020 20020022 c 20100001 109fc0 139fc3 8021 2012000c 24160003 26100001
  //   3210000f 20080008 20090001 139900 2709825 132020 20020022 c 1094022 1500fff9 22100001 2018000f
  //   2188024 108700 20080008 20090001 139902 2709825 132021 20020022 c 1094022 1500fff9 108702 2c9b022
  //   12c00001 8000050 4020 1084027 84400 3508ffff 82021 20020022 c 2010ffff 20110000 ae300000 22100001
  //   22310004 ae300000 22100001 22310004 ae300000 22100001 22310004 ae300000 22100001 22310004 ae300000
  //   22100001 22310004 ae300000 22100001 22310004 ae300000 22100001 22310004 ae300000 22100001 22310004
  //   ae300000 22100001 22310004 ae300000 22100001 22310004 ae300000 22100001 22310004 ae300000 22100001
  //   22310004 ae300000 22100001 22310004 ae300000 22100001 22310004 ae300000 22100001 22310004 ae300000
  //   22100001 22310004 22100001 8020 2011003c 8e130000 8e340000 274402a 11000002 ae330000 ae140000
  //   2231fffc 1611fff8 102020 20020022 c 22100004 2011003c 1611fff2 2002000a c 20100000 22100001 102020
  //   20020022 c 22100002 102020 20020022 c 22100003 102020 20020022 c 22100004 102020 20020022 c 22100005
  //   102020 20020022 c 22100006 102020 20020022 c 22100007 102020 20020022 c 22100008 102020 20020022
  //   20020022 c 3e00008
endmodule

module controller (
  input  [5:0] opcode,
  input  [5:0] funcode,
  input  CMP_RESULT,
  input  EQUAL_RESULT,
  output [1:0] regdatamux,
  output [1:0] regaddrmux,
  output regwrite_enable,
  output [1:0] pcmux,
  output isIMM,
  output memstore,
  output memload,
  output half_mem,
  output [3:0] alu_op,
  output syscall,
  output uncond_jmp,
  output cond_jmp,
  output succ_cond_jmp
);

  wire and_1_out, and_2_out, and_3_out, beq, bltz, bne, comparator_1_eq, comparator_2_eq, decoder_1_out8,
       decoder_1_out9, decoder_1_out10, decoder_1_out11, decoder_1_out12, decoder_1_out13, decoder_1_out14,
       decoder_1_out15, decoder_1_out16, decoder_1_out24, f0, imm_type, j, jr, lw, not_1_out, not_2_out,
       or_4_out, R_type;
  wire [1:0] priority_encoder_2_out;
  wire [3:0] fun2alu_1_out_2, op2alu_1_out_2;

  or or_1 (memload, half_mem, lw);
  op2alu op2alu_1 (.funcode(opcode), .out_2(op2alu_1_out_2));
  fun2alu fun2alu_1 (.funcode(funcode), .out_2(fun2alu_1_out_2));
  Multiplexer #(.width(4), .enable("false")) multiplexer_1 (
    .in0(op2alu_1_out_2), .in1(fun2alu_1_out_2), .out(alu_op), .sel(f0));
  or or_2 (isIMM, imm_type, half_mem, lw, memstore);
  and and_1 (and_1_out, bne, not_1_out);
  not not_1 (not_1_out, EQUAL_RESULT);
  and and_2 (and_2_out, beq, EQUAL_RESULT);
  and and_3 (and_3_out, CMP_RESULT, bltz);
  Decoder #(.select(5), .disabled(0), .enable("false")) decoder_1 (
    .out0(f0), .out1(bltz), .out2(j), .out3(regaddrmux[1]), .out4(beq), .out5(bne), .out8(decoder_1_out8),
    .out9(decoder_1_out9), .out10(decoder_1_out10), .out11(decoder_1_out11), .out12(decoder_1_out12),
    .out13(decoder_1_out13), .out14(decoder_1_out14), .out15(decoder_1_out15), .out16(decoder_1_out16),
    .out17(half_mem), .out19(lw), .out24(decoder_1_out24), .out27(memstore), .sel({opcode[5], opcode[3:0]}));  // open: out6, out7, out18, out20, out21, out22, out23, out25, out26, out28, out29, out30, out31
  Comparator #(.width(6), .mode("unsigned")) comparator_1 (
    .a(6'b001100), .b(funcode), .eq(comparator_1_eq));  // open: gt, lt
  Comparator #(.width(6), .mode("unsigned")) comparator_2 (
    .a(funcode), .b(6'b001000), .eq(comparator_2_eq));  // open: gt, lt
  not not_2 (not_2_out, f0);
  Priority_Encoder priority_encoder_1 (
    .in0(decoder_1_out8), .in1(decoder_1_out9), .in2(decoder_1_out10), .in3(decoder_1_out11),
    .in4(decoder_1_out12), .in5(decoder_1_out13), .in6(decoder_1_out14), .in7(decoder_1_out15), .gs(imm_type));  // open: out, en_in, en_out
  Decoder #(.select(2), .enable("false")) decoder_2 (
    .out0(R_type), .out1(syscall), .out2(jr), .sel(priority_encoder_2_out));  // open: out3
  Priority_Encoder #(.select(2), .disabled(0)) priority_encoder_2 (
    .in0(1'b1), .in1(comparator_1_eq), .in2(comparator_2_eq), .in3(not_2_out), .out(priority_encoder_2_out));  // open: gs, en_out, en_in
  or or_3 (succ_cond_jmp, and_1_out, and_2_out, and_3_out);
  or or_4 (or_4_out, regaddrmux[1], j);
  or or_5 (regwrite_enable, imm_type, R_type, lw, half_mem, regaddrmux[1]);
  Priority_Encoder #(.select(2), .disabled(0)) priority_encoder_3 (
    .in0(1'b1), .in1(jr), .in2(succ_cond_jmp), .in3(or_4_out), .out(pcmux));  // open: gs, en_out, en_in
  or or_6 (cond_jmp, bne, beq, bltz);
  or or_7 (uncond_jmp, jr, regaddrmux[1], j);

  assign regaddrmux[0] = isIMM;
  assign regdatamux = {memload, regaddrmux[1]};

  // Other names for the same wires on the sheet: aluop[3:0] = alu_op; lh = half_mem; jal = regaddrmux[1];
  //   sw = memstore
endmodule

module op2alu (
  input  [5:0] funcode,
  output [3:0] out_2
);

  wire and_1_out, and_2_out, and_3_out, and_4_out, and_5_out, and_6_out, and_7_out, not_1_out, not_2_out,
       not_3_out, not_4_out, not_5_out, not_6_out, not_7_out, not_8_out, not_9_out, or_1_out, or_2_out,
       or_3_out;

  or or_1 (or_1_out, funcode[5], funcode[3]);
  not not_1 (not_1_out, or_1_out);
  or or_2 (or_2_out, not_1_out, funcode[2]);
  or or_3 (or_3_out, not_1_out, funcode[1]);
  not not_2 (not_2_out, funcode[0]);
  not not_3 (not_3_out, or_3_out);
  not not_4 (not_4_out, funcode[0]);
  not not_5 (not_5_out, or_2_out);
  not not_6 (not_6_out, funcode[0]);
  not not_7 (not_7_out, funcode[0]);
  not not_8 (not_8_out, or_2_out);
  not not_9 (not_9_out, funcode[0]);
  and and_1 (and_1_out, or_3_out, not_2_out);
  and and_2 (and_2_out, or_2_out, funcode[0]);
  and and_3 (and_3_out, not_3_out, not_4_out);
  and and_4 (and_4_out, not_5_out, funcode[0]);
  and and_5 (and_5_out, or_3_out, not_6_out);
  and and_6 (and_6_out, or_2_out, not_7_out);
  and and_7 (and_7_out, or_2_out, or_3_out);
  or or_4 (out_2[0], not_8_out, not_9_out, or_3_out);
  or or_5 (out_2[3], and_1_out, and_2_out);
  or or_6 (out_2[2], and_3_out, and_4_out);
  or or_7 (out_2[1], and_5_out, and_6_out, and_7_out);
endmodule

module fun2alu (
  input  [5:0] funcode,
  output [3:0] out_2
);

  wire and_1_out, and_2_out, and_3_out, and_4_out, and_5_out, and_6_out, and_7_out, and_8_out, and_9_out,
       and_10_out, and_11_out, not_1_out, not_2_out, not_3_out, not_4_out, not_5_out, not_6_out, not_7_out,
       not_8_out, not_9_out, not_10_out, not_11_out, not_12_out, not_13_out, not_14_out, not_15_out,
       not_16_out, not_17_out, or_1_out, or_2_out;

  not not_1 (not_1_out, funcode[5]);
  or or_1 (or_1_out, not_1_out, funcode[3]);
  or or_2 (or_2_out, not_1_out, funcode[2]);
  not not_2 (not_2_out, or_1_out);
  not not_3 (not_3_out, or_2_out);
  not not_4 (not_4_out, or_1_out);
  not not_5 (not_5_out, funcode[0]);
  not not_6 (not_6_out, or_2_out);
  not not_7 (not_7_out, or_1_out);
  not not_8 (not_8_out, funcode[0]);
  not not_9 (not_9_out, or_1_out);
  not not_10 (not_10_out, funcode[0]);
  not not_11 (not_11_out, or_1_out);
  not not_12 (not_12_out, funcode[1]);
  not not_13 (not_13_out, funcode[0]);
  not not_14 (not_14_out, or_2_out);
  not not_15 (not_15_out, funcode[1]);
  not not_16 (not_16_out, or_2_out);
  not not_17 (not_17_out, funcode[0]);
  and and_1 (and_1_out, not_2_out, or_2_out, funcode[0]);
  or or_3 (out_2[3], and_1_out, and_2_out);
  and and_2 (and_2_out, or_1_out, not_3_out);
  and and_3 (and_3_out, not_4_out, not_5_out);
  or or_4 (out_2[2], and_3_out, and_4_out);
  and and_4 (and_4_out, not_6_out, funcode[0]);
  and and_5 (and_5_out, not_7_out, funcode[1]);
  and and_6 (and_6_out, funcode[1], not_8_out);
  or or_5 (out_2[1], and_5_out, and_6_out, and_7_out);
  and and_7 (and_7_out, not_9_out, or_2_out, not_10_out);
  and and_8 (and_8_out, not_11_out, not_12_out, not_13_out);
  and and_9 (and_9_out, not_14_out, not_15_out);
  and and_10 (and_10_out, or_1_out, not_16_out, not_17_out);
  and and_11 (and_11_out, or_1_out, or_2_out, funcode[0]);
  or or_6 (out_2[0], and_8_out, and_9_out, and_10_out, and_11_out);
endmodule
