// Logisim project alu-test.circ as structural Verilog: 2 circuits, main circuit main
module main (
  output Signed_Overflow,
  output Unsigned_overflow,
  output [31:0] Result,
  output Equal,
  output [31:0] Result_2
);

  wire clock_1_out;
  wire [3:0] rom_3_data;
  wire [7:0] adder_1_out, register_1_q;
  wire [31:0] rom_1_data, rom_2_data;

  Clock clock_1 (.out(clock_1_out));
  Adder adder_1 (.a(8'h1), .b(register_1_q), .out(adder_1_out));  // open: cin, cout
  Register register_1 (.D(adder_1_out), .Q(register_1_q), .clk(clock_1_out));  // open: en, clr
  // Probe on register_1_q
  // Probe on rom_1_data
  ROM #(.dataWidth(32)) rom_1 (.addr(register_1_q), .data(rom_1_data));  // open: sel
  ROM #(.dataWidth(32)) rom_2 (.addr(register_1_q), .data(rom_2_data));  // open: sel
  // Probe on rom_2_data
  ROM #(.dataWidth(4)) rom_3 (.addr(register_1_q), .data(rom_3_data));  // open: sel
  ALU alu_1 (
    .AluOP(rom_3_data), .X(rom_1_data), .Equal(Equal), .Result(Result), .Signed_Overflow(Signed_Overflow),
    .Y(rom_2_data), .Result_2(Result_2), .UnSigned_Overflow(Unsigned_overflow));
  // Probe on Result
  // Probe on Result_2

  // Notes on the sheet:
  //   此电路用于检测学生设计的ALU部件封装是否符合要求
  //   当电路设计完成后，蓝色线红色不应该出现，输出也不应该是高阻态
  //   ROM中可以存放测试用例，使用时钟驱动调出不同的X，Y，S值进行批量验证
  //   封装的ALU应该正好放置于此
endmodule

module test (
  input  [31:0] X,
  input  [31:0] Y,
  input  [3:0] ALUOP,
  output Signed_Overflow,
  output Unsigned_overflow,
  output [31:0] Result,
  output Equal,
  output [31:0] Result_2
);


  // Notes on the sheet:
  //   封装的ALU应该正好放置于此
  //   此电路用于检测学生设计的ALU部件封装是否符合要求
  //   蓝色线红色不应该出现，输出也不应该是高阻态
endmodule
